// Logisim project s-mips.circ as structural Verilog: 24 circuits, main circuit S-MIPS Board
module S_MIPS_Board (
  input  DESHABILITAR_DISPATCHER,
  output halt
);

  wire button_1_out, CLK, CS, d_ff_1_q, LCLR, LoadRAM, LoadRAMOn, LW, R_R_W, R_W, ram_dispatcher_1_finished,
       RCS, Reset_out, RST, TTY_EN;
  wire [2:0] KDB;
  wire [3:0] LMask, Mask, ram_1_read_time, ram_1_write_time, RMask;
  wire [6:0] KDB_DATA, TTY_DATA;
  wire [15:0] Addr, LAddr, RAddr;
  wire [31:0] I0, I1, I2, I3, LData, ram_1_data_out_0, ram_1_data_out_1, ram_1_data_out_2, ram_1_data_out_3,
       RI0, RI1, RI2, RI3;

  TTY #(.rows(25), .cols(80)) tty_1 (.data(TTY_DATA), .clk(CLK), .we(TTY_EN), .clr(RST));
  not not_1 (LoadRAMOn, ram_dispatcher_1_finished);
  RAM_Dispatcher ram_dispatcher_1 (
    .WriteTime(ram_1_write_time), .Clock(CLK), .Data(LData), .Address(LAddr), .Mask(LMask),
    .Finished(ram_dispatcher_1_finished), .Write(LW), .CLR(LCLR));
  Keyboard #(.buflen(64)) keyboard_1 (.clk(CLK), .re(KDB[0]), .avail(KDB[2]), .data(KDB_DATA));  // open: clr
  RAM ram_1 (
    .Address(RAddr), .Data_Out_0(ram_1_data_out_0), .Data_Out_1(ram_1_data_out_1),
    .Data_Out_2(ram_1_data_out_2), .Data_Out_3(ram_1_data_out_3), .Data_In_0(RI0), .Data_In_1(RI1),
    .Data_In_2(RI2), .Data_In_3(RI3), .Mask(RMask), .nRead_Write(R_R_W), .Chip_Select(RCS),
    .Read_Time(ram_1_read_time), .Reset(button_1_out), .Write_Time(ram_1_write_time));
  Button button_1 (.out(button_1_out));
  D_Flip_Flop d_ff_1 (.clk(CLK), .D(1'b1), .Q(d_ff_1_q), .reset(Reset_out));  // open: Qn, preset, en
  Button Reset (.out(Reset_out));
  S_MIPS s_mips_1 (
    .Kbd_Enable(KDB[0]), .Address(Addr), .Kbd_Clear(KDB[1]), .Kbd_Available(KDB[2]), .RAM_In_0(I0),
    .Kbd_ASCII_Data(KDB_DATA), .RAM_In_1(I1), .TTY_Enable(TTY_EN), .RAM_In_2(I2), .RAM_In_3(I3),
    .TTY_ASCII_Data(TTY_DATA), .Reset(RST), .RAM_Out_0(ram_1_data_out_0), .Clock(CLK),
    .RAM_Out_1(ram_1_data_out_1), .Stop(halt), .RAM_Out_2(ram_1_data_out_2), .RAM_Out_3(ram_1_data_out_3),
    .Mask(Mask), .Read_Time(ram_1_read_time), .Write_Time(ram_1_write_time), .nRead_Write(R_W),
    .Chip_Select(CS));
  D_Flip_Flop d_ff_2 (.clk(CLK), .D(d_ff_1_q), .Qn(LCLR), .reset(Reset_out));  // open: Q, preset, en
  or or_1 (RST, LCLR, LoadRAM);
  Clock clock_1 (.out(CLK));
  Multiplexer #(.width(32), .enable("false")) multiplexer_1 (.in0(I0), .in1(LData), .out(RI0), .sel(LoadRAM));
  Multiplexer #(.width(32), .enable("false")) multiplexer_2 (.in0(I1), .in1(LData), .out(RI1), .sel(LoadRAM));
  Multiplexer #(.width(32), .enable("false")) multiplexer_3 (.in0(I2), .in1(LData), .out(RI2), .sel(LoadRAM));
  Multiplexer #(.width(32), .enable("false")) multiplexer_4 (.in0(I3), .in1(LData), .out(RI3), .sel(LoadRAM));
  and and_1 (LoadRAM, ~DESHABILITAR_DISPATCHER, LoadRAMOn);  // AND_Gate
  Multiplexer #(.width(16), .enable("false")) multiplexer_5 (.in0(Addr), .in1(LAddr), .out(RAddr), .sel(LoadRAM));
  Multiplexer #(.width(4), .enable("false")) multiplexer_6 (.in0(Mask), .in1(LMask), .out(RMask), .sel(LoadRAM));
  Multiplexer #(.enable("false")) multiplexer_7 (.in0(CS), .in1(LW), .out(RCS), .sel(LoadRAM));
  Multiplexer #(.enable("false")) multiplexer_8 (.in0(R_W), .in1(LW), .out(R_R_W), .sel(LoadRAM));

  // Notes on the sheet:
  //   NO MODIFICAR
  //   Keyboard
endmodule

module RAM (
  input  [15:0] Address,
  input  [31:0] Data_In_0,
  input  [31:0] Data_In_1,
  input  [31:0] Data_In_2,
  input  [31:0] Data_In_3,
  input  [3:0] Mask,
  input  nRead_Write,
  input  Chip_Select,
  input  Reset,
  output [31:0] Data_Out_0,
  output [31:0] Data_Out_1,
  output [31:0] Data_Out_2,
  output [31:0] Data_Out_3,
  output [3:0] Read_Time,
  output [3:0] Write_Time
);

  wire and_2_out, and_3_out, and_4_out, and_5_out, and_6_out, and_7_out, and_8_out, and_9_out, Changed, CLK,
       comparator_2_eq, comparator_3_eq, comparator_4_eq, comparator_5_eq, comparator_6_eq, Count,
       demultiplexer_3_out0, Idle, Idle_q, Load, Load0, Load1, nand_1_out, or_1_out, or_2_out, or_3_out,
       or_4_out, or_5_out, or_6_out, or_7_out, or_8_out, or_9_out, or_10_out, Proc_q, Update_Mem, Zero_Time;
  wire [3:0] counter_1_q, multiplexer_1_out, subtractor_1_out;
  wire [31:0] register_1_q, register_2_q, register_3_q, register_4_q, register_5_q;

  // Probe on 4'b0101
  // Probe on 4'b0011
  Multiplexer #(.width(4), .enable("false")) multiplexer_1 (
    .in0(4'b0101), .in1(4'b0011), .out(multiplexer_1_out), .sel(nRead_Write));
  or or_1 (or_1_out, Idle, Update_Mem);
  or or_2 (or_2_out, ~Chip_Select, Reset);  // OR_Gate
  Subtractor #(.width(4)) subtractor_1 (.a(multiplexer_1_out), .b(4'b0010), .out(subtractor_1_out));  // open: bin, bout
  Demultiplexer #(.enable("false")) demultiplexer_1 (.out0(Idle), .out1(Load0), .in(Idle_q), .sel(Changed));
  D_Flip_Flop u_Idle (.clk(CLK), .D(or_1_out), .Q(Idle_q), .preset(or_2_out));  // open: Qn, en, reset
  // Probe on counter_1_q
  Counter #(.width(4), .max('hf)) counter_1 (
    .load(Load), .D(subtractor_1_out), .count(Count), .Q(counter_1_q), .clk(CLK), .clr(or_3_out));  // open: carry
  or or_3 (or_3_out, ~Chip_Select, Reset);  // OR_Gate
  Comparator #(.width(4), .mode("unsigned")) comparator_1 (
    .a(4'b0000), .b(counter_1_q), .eq(Zero_Time));  // open: gt, lt
  or or_4 (or_4_out, Count, Load0, Load1);
  Register #(.width(32)) register_1 (.D(Data_In_0), .en(Chip_Select), .Q(register_1_q), .clk(CLK), .clr(or_5_out));
  or or_5 (or_5_out, ~Chip_Select, Reset);  // OR_Gate
  Register #(.width(32)) register_2 (.D(Data_In_1), .en(Chip_Select), .Q(register_2_q), .clk(CLK), .clr(or_6_out));
  or or_6 (or_6_out, ~Chip_Select, Reset);  // OR_Gate
  Register #(.width(32)) register_3 (.D(Data_In_2), .en(Chip_Select), .Q(register_3_q), .clk(CLK), .clr(or_7_out));
  or or_7 (or_7_out, ~Chip_Select, Reset);  // OR_Gate
  Register #(.width(32)) register_4 (.D(Data_In_3), .en(Chip_Select), .Q(register_4_q), .clk(CLK), .clr(or_8_out));
  or or_8 (or_8_out, ~Chip_Select, Reset);  // OR_Gate
  Register #(.width(32)) register_5 (
    .D({{11{1'b1}}, nRead_Write, Mask, Address}), .en(Chip_Select), .Q(register_5_q), .clk(CLK),
    .clr(or_9_out));
  or or_9 (or_9_out, ~Chip_Select, Reset);  // OR_Gate
  D_Flip_Flop Proc (.clk(CLK), .D(or_4_out), .Q(Proc_q), .reset(or_10_out));  // open: Qn, preset, en
  or or_10 (or_10_out, ~Chip_Select, Reset);  // OR_Gate
  Demultiplexer #(.enable("false")) demultiplexer_2 (
    .out0(Count), .out1(Update_Mem), .in(demultiplexer_3_out0), .sel(Zero_Time));
  Demultiplexer #(.enable("false")) demultiplexer_3 (
    .out0(demultiplexer_3_out0), .out1(Load1), .in(Proc_q), .sel(Changed));
  Clock clock_1 (.out(CLK));
  Comparator #(.width(32)) comparator_2 (.a(register_1_q), .b(Data_In_0), .eq(comparator_2_eq));  // open: gt, lt
  Comparator #(.width(32)) comparator_3 (.a(register_2_q), .b(Data_In_1), .eq(comparator_3_eq));  // open: gt, lt
  Comparator #(.width(32)) comparator_4 (.a(register_3_q), .b(Data_In_2), .eq(comparator_4_eq));  // open: gt, lt
  Comparator #(.width(32)) comparator_5 (.a(register_4_q), .b(Data_In_3), .eq(comparator_5_eq));  // open: gt, lt
  Comparator #(.width(32)) comparator_6 (
    .a(register_5_q), .b({{11{1'b1}}, nRead_Write, Mask, Address}), .eq(comparator_6_eq));  // open: gt, lt
  nand nand_1 (nand_1_out, comparator_6_eq, comparator_2_eq, comparator_3_eq, comparator_4_eq, comparator_5_eq);
  and and_1 (Changed, nand_1_out, Chip_Select);
  or or_11 (Load, Count, Load1, Load0);
  and and_2 (and_2_out, Mask[0], Update_Mem, nRead_Write);
  and and_3 (and_3_out, Mask[1], Update_Mem, nRead_Write);
  and and_4 (and_4_out, Mask[2], Update_Mem, nRead_Write);
  and and_5 (and_5_out, Mask[3], Update_Mem, nRead_Write);
  RAM_part #(.addrWidth(16), .dataWidth(32), .bus("separate")) ram_1 (
    .addr(Address), .din(Data_In_0), .data(Data_Out_0), .str(and_2_out), .sel(Chip_Select), .clk(CLK),
    .ld(and_6_out), .clr(Reset));
  and and_6 (and_6_out, ~nRead_Write, Idle);  // AND_Gate
  RAM_part #(.addrWidth(16), .dataWidth(32), .bus("separate")) ram_2 (
    .addr(Address), .din(Data_In_1), .data(Data_Out_1), .str(and_3_out), .sel(Chip_Select), .clk(CLK),
    .ld(and_7_out), .clr(Reset));
  and and_7 (and_7_out, ~nRead_Write, Idle);  // AND_Gate
  RAM_part #(.addrWidth(16), .dataWidth(32), .bus("separate")) ram_3 (
    .addr(Address), .din(Data_In_2), .data(Data_Out_2), .str(and_4_out), .sel(Chip_Select), .clk(CLK),
    .ld(and_8_out), .clr(Reset));
  and and_8 (and_8_out, ~nRead_Write, Idle);  // AND_Gate
  RAM_part #(.addrWidth(16), .dataWidth(32), .bus("separate")) ram_4 (
    .addr(Address), .din(Data_In_3), .data(Data_Out_3), .str(and_5_out), .sel(Chip_Select), .clk(CLK),
    .ld(and_9_out), .clr(Reset));
  and and_9 (and_9_out, ~nRead_Write, Idle);  // AND_Gate

  assign Read_Time = 4'b0101;
  assign Write_Time = 4'b0011;

  // Other names for the same wires on the sheet: M0 = Mask[0]; M1 = Mask[1]; M2 = Mask[2]; M3 = Mask[3];
  //   RW = nRead_Write; CLR = Reset; CS = Chip_Select; Load2 = Count

  // Notes on the sheet:
  //   NO MODIFICAR
  //   excepto quizás los valores RT y WT
  //   BANK0
  //   BANK1
  //   BANK2
  //   BANK3
endmodule

module S_MIPS (
  input  Kbd_Available,
  input  [6:0] Kbd_ASCII_Data,
  input  [31:0] RAM_Out_0,
  input  [31:0] RAM_Out_1,
  input  Reset,
  input  [31:0] RAM_Out_2,
  input  Clock,
  input  [31:0] RAM_Out_3,
  input  [3:0] Read_Time,
  input  [3:0] Write_Time,
  output Kbd_Enable,
  output [15:0] Address,
  output Kbd_Clear,
  output TTY_Enable,
  output [6:0] TTY_ASCII_Data,
  output Stop,
  output [31:0] RAM_In_0,
  output [31:0] RAM_In_1,
  output [31:0] RAM_In_2,
  output [31:0] RAM_In_3,
  output [3:0] Mask,
  output nRead_Write,
  output Chip_Select
);

  wire AluInst, d_ff_2_q, enGI, enPC, enRF, getData, getInst, Halt, JmpInst, MemInst, or_1_out, or_2_out,
       ReadyData, ReadyInst, ReadyW, Special_Inst, StackInst, Start, Tty, Write, WriteInst;
  wire [31:0] Address_t, data_path_1_rout, multiplexer_1_out, multiplexer_2_out, multiplexer_3_out,
       multiplexer_4_out, multiplexer_5_out, using_ram_1_out_14, using_ram_1_out_15, using_ram_1_out_16,
       using_ram_1_out_17;

  or or_1 (or_1_out, StackInst, MemInst);
  D_Flip_Flop #(.trigger("falling")) d_ff_1 (.clk(Clock), .D(Reset), .Q(Start));  // open: Qn, preset, en, reset
  Multiplexer #(.width(32)) multiplexer_1 (
    .in0(RAM_Out_0), .in1(RAM_In_0), .out(multiplexer_1_out), .sel(Write));  // open: en
  Multiplexer #(.width(32)) multiplexer_2 (
    .in0(RAM_Out_1), .in1(RAM_In_0), .out(multiplexer_2_out), .sel(Write));  // open: en
  Multiplexer #(.width(32)) multiplexer_3 (
    .in0(RAM_Out_2), .in1(RAM_In_0), .out(multiplexer_3_out), .sel(Write));  // open: en
  Multiplexer #(.width(32)) multiplexer_4 (
    .in0(RAM_Out_3), .in1(RAM_In_0), .out(multiplexer_4_out), .sel(Write));  // open: en
  Using_RAM using_ram_1 (
    .in_1(multiplexer_1_out), .in_2(multiplexer_2_out), .in_3(multiplexer_3_out), .in_4(multiplexer_4_out),
    .in_5(Address_t), .in_7(Read_Time), .in_6(Write_Time), .in_8(Clock), .in_9(Reset), .in_10(Write),
    .in_11(getInst), .in_12(getData), .is_inst(enGI), .out_14(using_ram_1_out_14),
    .out_15(using_ram_1_out_15), .out_16(using_ram_1_out_16), .out_17(using_ram_1_out_17), .out_18(Address),
    .out_19(Mask), .out_20(nRead_Write), .out_21(Chip_Select), .out_22(ReadyInst), .out_23(ReadyData),
    .out_24(ReadyW));
  Control_Unit control_unit_1 (
    .CLK(Clock), .START(Start), .READY_INST(ReadyInst), .ALU_INST(AluInst), .R_INST(Special_Inst),
    .RST(Reset), .TTY_INST(Tty), .READY_DATA(ReadyData), .JMP_INST(JmpInst), .MEM_INST(or_1_out),
    .WRITE_INST(WriteInst), .READY_WRITE(ReadyW), .RF(enRF), .PC(enPC), .END(Stop), .GET_DATA(getData),
    .UseGI(enGI), .WRITE(Write), .TTY_EN(TTY_Enable), .GET_INST(getInst), .KBD_EN(Kbd_Enable));
  Multiplexer #(.select(2), .width(32), .enable("false")) multiplexer_5 (
    .in0(using_ram_1_out_14), .in1(using_ram_1_out_15), .in2(using_ram_1_out_16), .in3(using_ram_1_out_17),
    .out(multiplexer_5_out), .sel(Address_t[3:2]));
  D_Flip_Flop #(.trigger("falling")) d_ff_2 (
    .clk(Clock), .D(getInst), .Q(d_ff_2_q), .en(or_2_out));  // open: Qn, preset, reset
  or or_2 (or_2_out, getInst, ReadyInst);
  Data_Path data_path_1 (
    .clk(Clock), .rst(Reset), .kbd_Available(Kbd_Available), .Next_Instruction(d_ff_2_q), .RF(enRF),
    .enable_PC(enPC), .inst(multiplexer_5_out), .out_14(Halt), .out_15(AluInst), .out_10(Special_Inst),
    .out_11(JmpInst), .kbd_Data(Kbd_ASCII_Data), .out_16(Tty), .out_17(MemInst), .out_12(StackInst),
    .out_13(WriteInst), .Address(Address_t), .TtyData(TTY_ASCII_Data), .ROut(data_path_1_rout),
    .enable_GI(enGI));
  Inverter inverter_1 (.in_1(data_path_1_rout), .Output(RAM_In_0));

  assign Kbd_Clear = Reset;
  assign RAM_In_1 = RAM_In_0;
  assign RAM_In_2 = RAM_In_0;
  assign RAM_In_3 = RAM_In_0;

  // Other names for the same wires on the sheet: CLK = Clock; CS = Chip_Select; KBD_AVAIL = Kbd_Available;
  //   CLR = Reset; KBD_CLR = Reset; KBD_DATA[6:0] = Kbd_ASCII_Data; RAM_A[15:0] = Address; RAM_MASK[3:0] = Mask;
  //   RAM_OUTPUT_0[31:0] = RAM_Out_0; RAM_OUTPUT_1[31:0] = RAM_Out_1; RAM_OUTPUT_2[31:0] = RAM_Out_2;
  //   RAM_OUTPUT_3[31:0] = RAM_Out_3; RAM_INPUT_0[31:0] = RAM_In_0; RAM_INPUT_1[31:0] = RAM_In_0;
  //   RAM_INPUT_2[31:0] = RAM_In_0; RAM_INPUT_3[31:0] = RAM_In_0; ROut[31:0] = RAM_In_0; RW = nRead_Write;
  //   TTY_DATA[6:0] = TTY_ASCII_Data

  // Notes on the sheet:
  //   RAM ADDRESS
  //   DATA FROM RAM
  //   DATA TO RAM
  //   DATA WRITE MASK
  //   RAM TIMING
  //   RAM CONTROL
  //   KEYBOARD
  //   TTY
  //   SEQUENCING
  //   data
endmodule

module RAM_Dispatcher (
  input  [3:0] WriteTime,
  input  Clock,
  input  CLR,
  output [31:0] Data,
  output [15:0] Address,
  output [3:0] Mask,
  output Finished,
  output Write
);

  wire demultiplexer_2_out1, demultiplexer_3_out1, End, IDLE_q, IncAddr, Load, or_1_out, or_2_out, While_q,
       WriteEnd;
  wire [3:0] counter_1_q;
  wire [31:0] CurrentAddress_q;

  Counter #(.width(32), .max('hffffffff)) CurrentAddress (
    .count(IncAddr), .Q({CurrentAddress_q[31:18], Address, CurrentAddress_q[1:0]}), .clk(Clock), .clr(CLR));  // open: load, D, carry
  or or_1 (or_1_out, IncAddr, demultiplexer_3_out1, Finished);
  D_Flip_Flop IDLE (.clk(Clock), .D(or_1_out), .Q(IDLE_q), .preset(CLR));  // open: Qn, en, reset
  Demultiplexer #(.enable("false")) demultiplexer_1 (.out0(Load), .out1(Finished), .in(IDLE_q), .sel(End));
  D_Flip_Flop While (.clk(Clock), .D(or_2_out), .Q(While_q), .reset(CLR));  // open: Qn, preset, en
  or or_2 (or_2_out, Write, Load);
  RAM_part #(.addrWidth(18), .dataWidth(32)) ram_1 (
    .addr({Address, CurrentAddress_q[1:0]}), .data(Data), .clk(Clock));  // open: sel, ld, clr
  Demultiplexer #(.enable("false")) demultiplexer_2 (
    .out0(Write), .out1(demultiplexer_2_out1), .in(While_q), .sel(WriteEnd));
  Decoder #(.select(2)) decoder_1 (
    .out0(Mask[0]), .out1(Mask[1]), .out2(Mask[2]), .out3(Mask[3]), .sel(CurrentAddress_q[1:0]));  // open: en
  Demultiplexer #(.enable("false")) demultiplexer_3 (
    .out0(IncAddr), .out1(demultiplexer_3_out1), .in(demultiplexer_2_out1), .sel(End));
  Counter #(.width(4), .max('hf)) counter_1 (
    .load(Load), .D(WriteTime), .count(Write), .Q(counter_1_q), .clk(Clock));  // open: carry, clr
  Comparator #(.width(32)) comparator_1 (.a(Data), .b({32{1'b1}}), .eq(End));  // open: gt, lt
  Comparator #(.width(4)) comparator_2 (.a(4'b0000), .b(counter_1_q), .eq(WriteEnd));  // open: gt, lt

  // Other names for the same wires on the sheet: CLK = Clock; Count = Write; WT[3:0] = WriteTime
endmodule

module Register_File (
  input  [31:0] in,
  input  rst,
  input  clk,
  input  [4:0] select,
  input  [4:0] SA,
  input  [4:0] SB,
  input  Write,
  input  en_PC,
  input  Push,
  input  Pop,
  output [31:0] Out_A,
  output [31:0] Out_B,
  output [31:0] SP
);

  wire In31, L0, L1, L2, L3, L4, L5, L6, L7, L8, L9, L10, L11, L12, L13, L14, L15, L16, L17, L18, L19, L20,
       L21, L22, L23, L24, L25, L26, L27, L28, L29, L30, L31, or_1_out, or_2_out;
  wire [31:0] adder_1_out, multiplexer_2_out, multiplexer_4_out, Out0, Out1, Out2, Out3, Out4, Out5, Out6,
       Out7, Out8, Out9, Out10, Out11, Out12, Out13, Out14, Out15, Out16, Out17, Out18, Out19, Out20, Out21,
       Out22, Out23, Out24, Out25, Out26, Out27, Out28, Out29, Out30, SP_t, subtractor_1_out;

  Demultiplexer #(.select(5), .enable("false")) demultiplexer_1 (
    .out0(L0), .out1(L1), .out2(L2), .out3(L3), .out4(L4), .out5(L5), .out6(L6), .out7(L7), .out8(L8),
    .out9(L9), .out10(L10), .out11(L11), .out12(L12), .out13(L13), .out14(L14), .out15(L15), .out16(L16),
    .out17(L17), .out18(L18), .out19(L19), .out20(L20), .out21(L21), .out22(L22), .out23(L23), .out24(L24),
    .out25(L25), .out26(L26), .out27(L27), .out28(L28), .out29(L29), .out30(L30), .out31(In31), .in(Write),
    .sel(select));
  Register #(.width(32)) register_1 (.D({32{1'b0}}), .en(1'b1), .Q(Out0), .clk(clk), .clr(rst));
  Register #(.width(32)) register_2 (.D(in), .en(L6), .Q(Out6), .clk(clk), .clr(rst));
  Register #(.width(32)) register_3 (.D(in), .en(L12), .Q(Out12), .clk(clk), .clr(rst));
  Register #(.width(32)) register_4 (.D(in), .en(L18), .Q(Out18), .clk(clk), .clr(rst));
  Register #(.width(32)) register_5 (.D(in), .en(L24), .Q(Out24), .clk(clk), .clr(rst));
  Register #(.width(32)) register_6 (.D(in), .en(L30), .Q(Out30), .clk(clk), .clr(rst));
  Multiplexer #(.select(5), .width(32), .enable("false")) multiplexer_1 (
    .in0(Out0), .in1(Out1), .in2(Out2), .in3(Out3), .in4(Out4), .in5(Out5), .in6(Out6), .in7(Out7),
    .in8(Out8), .in9(Out9), .in10(Out10), .in11(Out11), .in12(Out12), .in13(Out13), .in14(Out14),
    .in15(Out15), .in16(Out16), .in17(Out17), .in18(Out18), .in19(Out19), .in20(Out20), .in21(Out21),
    .in22(Out22), .in23(Out23), .in24(Out24), .in25(Out25), .in26(Out26), .in27(Out27), .in28(Out28),
    .in29(Out29), .in30(Out30), .in31(SP), .out(Out_A), .sel(SA));
  Register #(.width(32)) register_7 (.D(in), .en(L1), .Q(Out1), .clk(clk), .clr(rst));
  Register #(.width(32)) register_8 (.D(in), .en(L7), .Q(Out7), .clk(clk), .clr(rst));
  Register #(.width(32)) register_9 (.D(in), .en(L13), .Q(Out13), .clk(clk), .clr(rst));
  Register #(.width(32)) register_10 (.D(in), .en(L19), .Q(Out19), .clk(clk), .clr(rst));
  Register #(.width(32)) register_11 (.D(in), .en(L25), .Q(Out25), .clk(clk), .clr(rst));
  Multiplexer #(.width(32), .enable("false")) multiplexer_2 (.in0(SP_t), .in1(in), .out(multiplexer_2_out), .sel(In31));
  Multiplexer #(.select(5), .width(32), .enable("false")) multiplexer_3 (
    .in0(Out0), .in1(Out1), .in2(Out2), .in3(Out3), .in4(Out4), .in5(Out5), .in6(Out6), .in7(Out7),
    .in8(Out8), .in9(Out9), .in10(Out10), .in11(Out11), .in12(Out12), .in13(Out13), .in14(Out14),
    .in15(Out15), .in16(Out16), .in17(Out17), .in18(Out18), .in19(Out19), .in20(Out20), .in21(Out21),
    .in22(Out22), .in23(Out23), .in24(Out24), .in25(Out25), .in26(Out26), .in27(Out27), .in28(Out28),
    .in29(Out29), .in30(Out30), .in31(SP), .out(Out_B), .sel(SB));
  Register #(.width(32)) register_12 (.D(in), .en(L2), .Q(Out2), .clk(clk), .clr(rst));
  Register #(.width(32)) register_13 (.D(in), .en(L8), .Q(Out8), .clk(clk), .clr(rst));
  Register #(.width(32)) register_14 (.D(in), .en(L14), .Q(Out14), .clk(clk), .clr(rst));
  Register #(.width(32)) register_15 (.D(in), .en(L20), .Q(Out20), .clk(clk), .clr(rst));
  Register #(.width(32)) register_16 (.D(in), .en(L26), .Q(Out26), .clk(clk), .clr(rst));
  or or_1 (or_1_out, L31, In31, rst);
  Register #(.width(32)) u_SP (.D(multiplexer_2_out), .en(or_1_out), .Q(SP), .clk(clk));  // open: clr
  Register #(.width(32)) register_17 (.D(in), .en(L3), .Q(Out3), .clk(clk), .clr(rst));
  Register #(.width(32)) register_18 (.D(in), .en(L9), .Q(Out9), .clk(clk), .clr(rst));
  Register #(.width(32)) register_19 (.D(in), .en(L15), .Q(Out15), .clk(clk), .clr(rst));
  Register #(.width(32)) register_20 (.D(in), .en(L21), .Q(Out21), .clk(clk), .clr(rst));
  Register #(.width(32)) register_21 (.D(in), .en(L27), .Q(Out27), .clk(clk), .clr(rst));
  and and_1 (L31, en_PC, or_2_out);
  or or_2 (or_2_out, Push, Pop);
  Subtractor #(.width(32)) subtractor_1 (.a(SP), .b(32'h4), .out(subtractor_1_out));  // open: bin, bout
  Adder #(.width(32)) adder_1 (.a(32'h4), .b(SP), .out(adder_1_out));  // open: cin, cout
  Register #(.width(32)) register_22 (.D(in), .en(L4), .Q(Out4), .clk(clk), .clr(rst));
  Register #(.width(32)) register_23 (.D(in), .en(L10), .Q(Out10), .clk(clk), .clr(rst));
  Register #(.width(32)) register_24 (.D(in), .en(L16), .Q(Out16), .clk(clk), .clr(rst));
  Register #(.width(32)) register_25 (.D(in), .en(L22), .Q(Out22), .clk(clk), .clr(rst));
  Register #(.width(32)) register_26 (.D(in), .en(L28), .Q(Out28), .clk(clk), .clr(rst));
  Multiplexer #(.width(32), .enable("false")) multiplexer_4 (
    .in0(subtractor_1_out), .in1(adder_1_out), .out(multiplexer_4_out), .sel(Pop));
  Multiplexer #(.width(32), .enable("false")) multiplexer_5 (
    .in0(multiplexer_4_out), .in1({32{1'b1}}), .out(SP_t), .sel(rst));
  Register #(.width(32)) register_27 (.D(in), .en(L5), .Q(Out5), .clk(clk), .clr(rst));
  Register #(.width(32)) register_28 (.D(in), .en(L11), .Q(Out11), .clk(clk), .clr(rst));
  Register #(.width(32)) register_29 (.D(in), .en(L17), .Q(Out17), .clk(clk), .clr(rst));
  Register #(.width(32)) register_30 (.D(in), .en(L23), .Q(Out23), .clk(clk), .clr(rst));
  Register #(.width(32)) register_31 (.D(in), .en(L29), .Q(Out29), .clk(clk), .clr(rst));

  // Other names for the same wires on the sheet: A[31:0] = Out_A; B[31:0] = Out_B; enPC = en_PC; Out31[31:0] = SP;
  //   Reset = rst

  // Notes on the sheet:
  //   Salidas
  //   Entradas
  //   Reg0
  //   Reg6
  //   Reg12
  //   Reg18
  //   Reg24
  //   Reg30
  //   Reg1
  //   Reg7
  //   Reg13
  //   Reg19
  //   Reg25
  //   Reg31 o SP
  //   Reg2
  //   Reg8
  //   Reg14
  //   Reg20
  //   Reg26
  //   Reg3
  //   Reg9
  //   Reg15
  //   Reg21
  //   Reg27
  //   SP cambia si la instr es pop/push
  //   Reg4
  //   Reg10
  //   Reg16
  //   Reg22
  //   Reg28
  //   Reg5
  //   Reg11
  //   Reg17
  //   Reg23
  //   Reg29
endmodule

module RF_Selector (
  input  in_1,
  input  [31:0] in_2,
  input  in_3,
  input  in_4,
  input  in_5,
  input  [31:0] in_6,
  input  in_7,
  input  in_8,
  input  [31:0] in_9,
  input  [31:0] in_10,
  input  [31:0] in_11,
  input  [6:0] Kbd_Data,
  output [31:0] out_13
);

  wire or_1_out;
  wire [2:0] Select;

  or or_1 (or_1_out, in_1, in_3);
  Priority_Encoder priority_encoder_1 (
    .in0(1'b1), .in1(or_1_out), .in2(in_4), .in3(in_5), .in4(in_8), .in5(in_7), .out(Select), .en_in(1'b1));  // open: in6, in7, gs, en_out
  Multiplexer #(.select(3), .width(32), .enable("false")) multiplexer_1 (
    .in0(in_2), .in1(in_9), .in2(in_10), .in3(in_11), .in4(in_6), .in5({{25{1'b0}}, Kbd_Data}), .out(out_13),
    .sel(Select));  // open: in6, in7

  // Other names for the same wires on the sheet: ALU[31:0] = in_2; HI[31:0] = in_10; isKbd = in_7; isRnd = in_8;
  //   Kbd[6:0] = Kbd_Data; LO[31:0] = in_11; Lw = in_1; Memory[31:0] = in_9; Mfhi = in_4; Mflo = in_5;
  //   OUT[31:0] = out_13; Pop = in_3; RND[31:0] = in_6

  // Notes on the sheet:
  //   Salida
  //   Entradas
  //   Prepara los datos que recibe el RF
endmodule

module ALU (
  input  [31:0] Op1,
  input  [31:0] Op2,
  input  [3:0] ALU_Select,
  input  in_4,
  input  in_5,
  output [31:0] OUT,
  output [31:0] OH,
  output [31:0] OL
);

  wire comparator_2_eq, Enable, less_than_1_less_than, mult;
  wire [31:0] ADD, AND, Div, DivRem, MUL_DIV, MultH, multiplexer_1_out, MultL, NOR, OR, SLT, SUB, XOR;

  Adder #(.width(32)) adder_1 (.a(Op1), .b(Op2), .out(ADD));  // open: cin, cout
  Subtractor #(.width(32)) subtractor_1 (.a(Op1), .b(Op2), .out(SUB));  // open: bin, bout
  assign AND = Op1 & Op2;  // AND_Gate and_1, 32 bits wide
  assign OR = Op1 | Op2;  // OR_Gate or_1, 32 bits wide
  assign NOR = ~(Op1 | Op2);  // NOR_Gate nor_1, 32 bits wide
  assign XOR = Op1 ^ Op2;  // XOR_Gate xor_1, 32 bits wide
  Comparator #(.width(4)) comparator_1 (.a(ALU_Select), .b(4'b0010), .eq(mult));  // open: gt, lt
  Comparator #(.width(4)) comparator_2 (.a(ALU_Select), .b(4'b0011), .eq(comparator_2_eq));  // open: gt, lt
  Less_Than less_than_1 (.A(Op1), .B(Op2), .sign(in_5), .Less_Than(less_than_1_less_than));
  or or_2 (Enable, mult, comparator_2_eq);
  assign SLT = {{31{1'b0}}, less_than_1_less_than};  // Bit_Extender bit_extender_1
  Multiplication multiplication_1 (.Sign(in_5), .A(Op1), .B(Op2), .OH(MultH), .OL(MultL));
  Division division_1 (.Op1(Op1), .Op2(Op2), .DivRem(DivRem), .Div(Div), .Sign(in_5));
  Multiplexer #(.width(32), .enable("false")) multiplexer_1 (
    .in0(DivRem), .in1(MultH), .out(multiplexer_1_out), .sel(mult));
  Multiplexer #(.select(4), .width(32), .enable("false")) multiplexer_2 (
    .in0(ADD), .in1(SUB), .in2(MUL_DIV), .in3(MUL_DIV), .in4(SLT), .in5(AND), .in6(OR), .in7(NOR), .in8(XOR),
    .out(OUT), .sel(ALU_Select));  // open: in9, in10, in11, in12, in13, in14, in15
  Register #(.width(32)) HIGH (.D(multiplexer_1_out), .en(Enable), .Q(OH), .clk(in_4));  // open: clr
  Multiplexer #(.width(32), .enable("false")) multiplexer_3 (.in0(Div), .in1(MultL), .out(MUL_DIV), .sel(mult));
  Register #(.width(32)) LOW (.D(MUL_DIV), .en(Enable), .Q(OL), .clk(in_4));  // open: clr

  // Other names for the same wires on the sheet: Clk = in_4; Select[3:0] = ALU_Select; Sign = in_5

  // Notes on the sheet:
  //   Salidas
  //   Entradas
  //   Se activa el enable si es mult o div
  //   Operaciones
  //   Trabajar con Hi y low
  //   Seleccionar la Salida
endmodule

module ALU_Selector (
  input  in_1,
  input  in_2,
  input  in_3,
  input  in_4,
  input  in_5,
  input  in_6,
  input  in_7,
  input  in_8,
  input  in_9,
  input  in_10,
  input  in_11,
  input  in_12,
  input  in_13,
  input  in_14,
  input  in_15,
  input  in_16,
  input  in_17,
  input  in_18,
  output Sign,
  output [3:0] Select,
  output I
);

  wire AND, DIV, MULT, OR, or_10_out, SLT, SLTI, XOR;

  or or_1 (Sign, in_5, in_3, in_7, in_14);
  or or_2 (I, in_14, in_13, in_16, in_18, in_17);
  or or_3 (DIV, in_5, in_6);
  or or_4 (MULT, in_3, in_4);
  or or_5 (SLT, in_7, in_8);
  or or_6 (SLTI, in_14, in_15);
  or or_7 (AND, in_9, in_16);
  or or_8 (OR, in_10, in_17);
  or or_9 (XOR, in_12, in_18);
  or or_10 (or_10_out, SLTI, SLT);
  Priority_Encoder #(.select(4)) priority_encoder_1 (
    .in0(1'b1), .in1(in_2), .in2(MULT), .in3(DIV), .in4(or_10_out), .in5(AND), .in6(OR), .in7(in_11),
    .in8(XOR), .out(Select), .en_in(1'b1));  // open: in9, in10, in11, in12, in13, in14, in15, gs, en_out

  // Other names for the same wires on the sheet: Add = in_1; Addi = in_13; And_t = in_9; Andi = in_16; Div_t = in_5;
  //   Divu = in_6; Mult_t = in_3; Mulu = in_4; Nor = in_11; Or_t = in_10; Ori = in_17; Slt_t = in_7; Slti_t = in_14;
  //   Sltiu = in_15; Sltu = in_8; Sub = in_2; Xor_t = in_12; Xori = in_18

  // Notes on the sheet:
  //   Prepara el selector que va a recibir la ALU
endmodule

module Instruction_Decoder (
  input  [31:0] \Instrucción ,
  output [25:0] out_2,
  output out_3,
  output out_4,
  output out_5,
  output out_6,
  output out_7,
  output out_8,
  output out_9,
  output out_10,
  output out_11,
  output out_12,
  output out_13,
  output out_14,
  output [15:0] out_15,
  output out_16,
  output out_17,
  output out_18,
  output out_19,
  output out_20,
  output [4:0] out_21,
  output out_22,
  output out_23,
  output out_24,
  output out_25,
  output out_26,
  output out_27,
  output out_28,
  output out_29,
  output out_30,
  output [4:0] out_31,
  output out_32,
  output out_33,
  output out_34,
  output out_35,
  output out_36,
  output [4:0] out_37,
  output out_38,
  output out_39,
  output out_40,
  output out_41,
  output out_42
);

  wire _000000, _111111, comparator_17_eq, comparator_18_eq, comparator_19_eq, comparator_20_eq,
       comparator_21_eq, comparator_22_eq, comparator_23_eq, comparator_24_eq, comparator_25_eq,
       comparator_26_eq, comparator_27_eq, comparator_28_eq, comparator_29_eq, comparator_30_eq,
       comparator_31_eq, comparator_32_eq, comparator_33_eq, comparator_34_eq, comparator_35_eq,
       comparator_36_eq, comparator_37_eq, comparator_38_eq, comparator_39_eq;

  Comparator #(.width(6)) comparator_1 (.a(\Instrucción [31:26]), .b({6{1'b1}}), .eq(_111111));  // open: gt, lt
  Comparator #(.width(6)) comparator_2 (.a(\Instrucción [31:26]), .b({6{1'b0}}), .eq(_000000));  // open: gt, lt
  Comparator #(.width(6)) comparator_3 (.a(\Instrucción [31:26]), .b(6'b001000), .eq(out_6));  // open: gt, lt
  Comparator #(.width(6)) comparator_4 (.a(\Instrucción [31:26]), .b(6'b001010), .eq(out_10));  // open: gt, lt
  Comparator #(.width(6)) comparator_5 (.a(\Instrucción [31:26]), .b(6'b001011), .eq(out_14));  // open: gt, lt
  Comparator #(.width(6)) comparator_6 (.a(\Instrucción [31:26]), .b(6'b001100), .eq(out_19));  // open: gt, lt
  Comparator #(.width(6)) comparator_7 (.a(\Instrucción [31:26]), .b(6'b001101), .eq(out_25));  // open: gt, lt
  Comparator #(.width(6)) comparator_8 (.a(\Instrucción [31:26]), .b(6'b001110), .eq(out_30));  // open: gt, lt
  Comparator #(.width(6)) comparator_9 (.a(\Instrucción [31:26]), .b(6'b100011), .eq(out_5));  // open: gt, lt
  Comparator #(.width(6)) comparator_10 (.a(\Instrucción [31:26]), .b(6'b101011), .eq(out_9));  // open: gt, lt
  Comparator #(.width(6)) comparator_11 (.a(\Instrucción [31:26]), .b(6'b000100), .eq(out_13));  // open: gt, lt
  Comparator #(.width(6)) comparator_12 (.a(\Instrucción [31:26]), .b(6'b000101), .eq(out_18));  // open: gt, lt
  Comparator #(.width(6)) comparator_13 (.a(\Instrucción [31:26]), .b(6'b000110), .eq(out_24));  // open: gt, lt
  Comparator #(.width(6)) comparator_14 (.a(\Instrucción [31:26]), .b(6'b000111), .eq(out_29));  // open: gt, lt
  Comparator #(.width(6)) comparator_15 (.a(\Instrucción [31:26]), .b(6'b000001), .eq(out_35));  // open: gt, lt
  Comparator #(.width(6)) comparator_16 (.a(\Instrucción [31:26]), .b(6'b000010), .eq(out_41));  // open: gt, lt
  Comparator #(.width(6)) comparator_17 (.a(\Instrucción [5:0]), .b({6{1'b0}}), .eq(comparator_17_eq));  // open: gt, lt
  Comparator #(.width(6)) comparator_18 (
    .a(\Instrucción [31:26]), .b(6'b111000), .eq(comparator_18_eq));  // open: gt, lt
  Comparator #(.width(6)) comparator_19 (.a(\Instrucción [5:0]), .b(6'b000001), .eq(comparator_19_eq));  // open: gt, lt
  and and_1 (out_20, _111111, comparator_20_eq);
  Comparator #(.width(6)) comparator_20 (.a(\Instrucción [5:0]), .b({6{1'b1}}), .eq(comparator_20_eq));  // open: gt, lt
  and and_2 (out_26, _111111, comparator_21_eq);
  Comparator #(.width(6)) comparator_21 (.a(\Instrucción [5:0]), .b(6'b000001), .eq(comparator_21_eq));  // open: gt, lt
  and and_3 (out_32, _111111, comparator_22_eq);
  Comparator #(.width(6)) comparator_22 (.a(\Instrucción [5:0]), .b(6'b000010), .eq(comparator_22_eq));  // open: gt, lt
  and and_4 (out_38, _111111, comparator_23_eq);
  Comparator #(.width(6)) comparator_23 (.a(\Instrucción [5:0]), .b(6'b000100), .eq(comparator_23_eq));  // open: gt, lt
  and and_5 (out_36, comparator_17_eq, comparator_18_eq);
  and and_6 (out_42, comparator_18_eq, comparator_19_eq);
  Comparator #(.width(6)) comparator_24 (.a(\Instrucción [5:0]), .b({6{1'b0}}), .eq(comparator_24_eq));  // open: gt, lt
  Comparator #(.width(6)) comparator_25 (.a(\Instrucción [5:0]), .b(6'b100000), .eq(comparator_25_eq));  // open: gt, lt
  Comparator #(.width(6)) comparator_26 (.a(\Instrucción [5:0]), .b(6'b100010), .eq(comparator_26_eq));  // open: gt, lt
  Comparator #(.width(6)) comparator_27 (.a(\Instrucción [5:0]), .b(6'b011000), .eq(comparator_27_eq));  // open: gt, lt
  Comparator #(.width(6)) comparator_28 (.a(\Instrucción [5:0]), .b(6'b011001), .eq(comparator_28_eq));  // open: gt, lt
  Comparator #(.width(6)) comparator_29 (.a(\Instrucción [5:0]), .b(6'b011010), .eq(comparator_29_eq));  // open: gt, lt
  Comparator #(.width(6)) comparator_30 (.a(\Instrucción [5:0]), .b(6'b011011), .eq(comparator_30_eq));  // open: gt, lt
  Comparator #(.width(6)) comparator_31 (.a(\Instrucción [5:0]), .b(6'b101010), .eq(comparator_31_eq));  // open: gt, lt
  and and_7 (out_3, _000000, comparator_24_eq);
  and and_8 (out_7, _000000, comparator_25_eq);
  and and_9 (out_11, _000000, comparator_26_eq);
  and and_10 (out_16, _000000, comparator_27_eq);
  and and_11 (out_22, _000000, comparator_28_eq);
  and and_12 (out_27, _000000, comparator_29_eq);
  and and_13 (out_33, _000000, comparator_30_eq);
  and and_14 (out_39, _000000, comparator_31_eq);
  Comparator #(.width(6)) comparator_32 (.a(\Instrucción [5:0]), .b(6'b101000), .eq(comparator_32_eq));  // open: gt, lt
  Comparator #(.width(6)) comparator_33 (.a(\Instrucción [5:0]), .b(6'b001000), .eq(comparator_33_eq));  // open: gt, lt
  Comparator #(.width(6)) comparator_34 (.a(\Instrucción [5:0]), .b(6'b010000), .eq(comparator_34_eq));  // open: gt, lt
  Comparator #(.width(6)) comparator_35 (.a(\Instrucción [5:0]), .b(6'b010010), .eq(comparator_35_eq));  // open: gt, lt
  Comparator #(.width(6)) comparator_36 (.a(\Instrucción [5:0]), .b(6'b100111), .eq(comparator_36_eq));  // open: gt, lt
  Comparator #(.width(6)) comparator_37 (.a(\Instrucción [5:0]), .b(6'b101011), .eq(comparator_37_eq));  // open: gt, lt
  Comparator #(.width(6)) comparator_38 (.a(\Instrucción [5:0]), .b(6'b100100), .eq(comparator_38_eq));  // open: gt, lt
  Comparator #(.width(6)) comparator_39 (.a(\Instrucción [5:0]), .b(6'b100101), .eq(comparator_39_eq));  // open: gt, lt
  and and_15 (out_23, _000000, comparator_32_eq);
  and and_16 (out_28, _000000, comparator_33_eq);
  and and_17 (out_34, _000000, comparator_34_eq);
  and and_18 (out_40, _000000, comparator_35_eq);
  and and_19 (out_17, _000000, comparator_36_eq);
  and and_20 (out_4, _000000, comparator_37_eq);
  and and_21 (out_8, _000000, comparator_38_eq);
  and and_22 (out_12, _000000, comparator_39_eq);

  assign out_2 = \Instrucción [25:0];
  assign out_15 = \Instrucción [15:0];
  assign out_21 = \Instrucción [25:21];
  assign out_31 = \Instrucción [20:16];
  assign out_37 = \Instrucción [15:11];

  // Other names for the same wires on the sheet: Add = out_7; Addi = out_6; And = out_8; Andi = out_19; Bgtz = out_29;
  //   Blez = out_24; Bltz = out_35; Bne = out_18; Bqe = out_13; Const[15:0] = \Instrucción [15:0];
  //   Dest[25:0] = \Instrucción [25:0]; FC[5:0] = \Instrucción [5:0]; RD[4:0] = \Instrucción [15:11];
  //   RT[4:0] = \Instrucción [20:16]; RS[4:0] = \Instrucción [25:21]; Div = out_27; Divu = out_33; Halt = out_20;
  //   J = out_41; Jr = out_28; Kbd = out_38; Lw = out_5; Mfhi = out_34; Mflo = out_40; Mult = out_16; Mulu = out_22;
  //   Nop = out_3; Nor = out_17; OP[5:0] = \Instrucción [31:26]; Or = out_12; Ori = out_25; Pop = out_36;
  //   Push = out_42; Rnd = out_32; Slt = out_39; Slti = out_10; Sltiu = out_14; Sltu = out_4; Sub = out_11;
  //   Sw = out_9; Tty = out_26; Xor = out_23; Xori = out_30

  // Notes on the sheet:
  //   OP-Code
  //   Separa la instrucción
  //   OP = 111111
  //   OP = 111000
  //   Salidas
  //   OP = 000000
endmodule

module Data_Path (
  input  kbd_Available,
  input  [31:0] inst,
  input  enable_PC,
  input  Next_Instruction,
  input  [6:0] kbd_Data,
  input  enable_GI,
  input  clk,
  input  RF,
  input  rst,
  output out_10,
  output out_11,
  output out_12,
  output out_13,
  output out_14,
  output out_15,
  output out_16,
  output out_17,
  output [6:0] TtyData,
  output [31:0] ROut,
  output [31:0] Address
);

  wire Add, Addi, And, Andi, Bgtz, Blez, Bltz, Bne, Bqe, Div, Divu, I, J, Jr, Kbd, Lw, Mfhi, Mflo, Mult,
       Mulu, Nop, Nor, Or, or_1_out, Ori, Pop, Push, Rnd, Sign, Slt, Slti, Sltiu, Sltu, Sub, Sw, Xor, Xori;
  wire [3:0] AluSelect;
  wire [4:0] multiplexer_3_out, RD, RS, RT;
  wire [15:0] Const;
  wire [25:0] Dest;
  wire [31:0] AluOut, const_ext_1_extended, g_instruction_1_output, HI, LO, multiplexer_1_out, PCIn, PCOut,
       random_1_out, rf_selector_1_out_13, RT_t, SP;
  wire [31:7] RS_t;

  or or_1 (or_1_out, Sw, Addi, Lw);
  G_Instruction g_instruction_1 (
    .in_1(inst), .Output(g_instruction_1_output), .in_2(enable_GI), .in_3(clk), .in_4(rst));
  Instruction_Decoder instruction_decoder_1 (
    .out_3(Nop), .out_4(Sltu), .out_5(Lw), .out_6(Addi), .out_21(RS), .\Instrucción (g_instruction_1_output),
    .out_7(Add), .out_8(And), .out_9(Sw), .out_10(Slti), .out_2(Dest), .out_31(RT), .out_11(Sub),
    .out_12(Or), .out_13(Bqe), .out_14(Sltiu), .out_37(RD), .out_16(Mult), .out_17(Nor), .out_18(Bne),
    .out_19(Andi), .out_15(Const), .out_22(Mulu), .out_23(Xor), .out_24(Blez), .out_25(Ori), .out_27(Div),
    .out_28(Jr), .out_29(Bgtz), .out_30(Xori), .out_33(Divu), .out_34(Mfhi), .out_35(Bltz), .out_39(Slt),
    .out_40(Mflo), .out_41(J), .out_36(Pop), .out_42(Push), .out_20(out_14), .out_26(out_16), .out_32(Rnd),
    .out_38(Kbd));
  ALU_Selector alu_selector_1 (
    .in_1(Add), .in_9(And), .in_17(Ori), .in_2(Sub), .in_10(Or), .in_18(Xori), .in_3(Mult), .in_11(Nor),
    .in_4(Mulu), .in_12(Xor), .in_5(Div), .in_13(or_1_out), .in_6(Divu), .in_14(Slti), .in_7(Slt),
    .in_15(Sltiu), .in_8(Sltu), .in_16(Andi), .Sign(Sign), .Select(AluSelect), .I(I));
  Const_Ext const_ext_1 (.ori(Ori), .andi(Andi), .\const (Const), .xori(Xori), .Extended(const_ext_1_extended));
  Multiplexer #(.width(32), .enable("false")) multiplexer_1 (
    .in0(RT_t), .in1(const_ext_1_extended), .out(multiplexer_1_out), .sel(I));
  ALU alu_1 (
    .Op1({RS_t, TtyData}), .Op2(multiplexer_1_out), .ALU_Select(AluSelect), .in_4(clk), .in_5(Sign),
    .OUT(AluOut), .OH(HI), .OL(LO));
  Branch_Control branch_control_1 (
    .Dest(Dest), .RS({RS_t, TtyData}), .RT(RT_t), .PC(PCOut), .Const(Const), .beq(Bqe), .bne(Bne),
    .blez(Blez), .bgtz(Bgtz), .bltz(Bltz), .jr(Jr), .j(J), .OUT(PCIn));
  Register #(.width(32)) PC (.D(PCIn), .en(enable_PC), .Q(PCOut), .clk(clk), .clr(rst));
  or or_2 (out_10, Rnd, Mfhi, Mflo, Kbd, out_16);
  or or_3 (out_13, Push, Sw);
  or or_4 (out_12, Push, Pop);
  Multiplexer #(.width(32), .enable("false")) multiplexer_2 (.in0({RS_t, TtyData}), .in1(RT_t), .out(ROut), .sel(Sw));
  Random #(.width(32)) random_1 (.clk(clk), .next(Rnd), .out(random_1_out));  // open: clr
  or or_5 (out_11, Bgtz, Bqe, Bne, Blez, Bltz, Jr, J, Nop);
  or or_6 (out_17, Lw, Sw);
  RF_Selector rf_selector_1 (
    .in_2(AluOut), .in_6(random_1_out), .in_9(inst), .in_10(HI), .in_11(LO), .Kbd_Data(kbd_Data), .in_1(Lw),
    .in_3(Pop), .in_4(Mfhi), .in_5(Mflo), .in_7(Kbd), .in_8(Rnd), .out_13(rf_selector_1_out_13));
  Memory_Address memory_address_1 (
    .PC(PCOut), .ALU(AluOut), .SP(SP), .LW(Lw), .SW(Sw), .POP(Pop), .PUSH(Push), .IS_PC(Next_Instruction),
    .OUT(Address));
  Multiplexer #(.width(5)) multiplexer_3 (.in0(RD), .in1(RT), .out(multiplexer_3_out), .sel(I));  // open: en
  Register_File register_file_1 (
    .in(rf_selector_1_out_13), .select(multiplexer_3_out), .SA(RS), .SB(RT), .Write(RF), .en_PC(enable_PC),
    .Push(Push), .Pop(Pop), .clk(clk), .rst(rst), .Out_B(RT_t), .SP(SP), .Out_A({RS_t, TtyData}));
  or or_7 (out_15, Xori, Add, Mult, And, Nor, Ori, Mulu, Sub, Xor, Div, Or, Addi, Slti, Divu, Slt, Sltiu, Sltu, Andi);

  // Other names for the same wires on the sheet: AluInst = out_15; enGI = enable_GI; enPC = enable_PC; enRF = RF;
  //   Halt = out_14; Instruction[31:0] = inst; JmpInst = out_11; KbdAva = kbd_Available; KbdData[6:0] = kbd_Data;
  //   MemInst = out_17; Nextl = Next_Instruction; Reset = rst; RInst = out_10; RS_t[6:0] = TtyData;
  //   StackInst = out_12; Tty = out_16; WriteInst = out_13

  // Notes on the sheet:
  //   Entradas
  //   Salidas
  //   Selecciona la salida
  //   Activa las instancias que se están usando
endmodule

module Control_Unit (
  input  CLK,
  input  TTY_INST,
  input  START,
  input  READY_DATA,
  input  READY_INST,
  input  JMP_INST,
  input  ALU_INST,
  input  MEM_INST,
  input  R_INST,
  input  WRITE_INST,
  input  RST,
  input  READY_WRITE,
  output RF,
  output GET_INST,
  output WRITE,
  output PC,
  output UseGI,
  output END,
  output TTY_EN,
  output GET_DATA,
  output KBD_EN
);

  wire Branch, d_ff_1_q, d_ff_2_q, d_ff_5_q, d_ff_6_q, demultiplexer_1_out1, Idle, or_2_out, RF_t;
  wire [2:0] Selector;

  Demultiplexer #(.select(3)) demultiplexer_1 (
    .out0(Idle), .out1(demultiplexer_1_out1), .out2(Branch), .out3(RF_t), .out4(GET_DATA), .out5(WRITE),
    .in(d_ff_1_q), .sel(Selector));  // open: out6, out7, en
  D_Flip_Flop #(.trigger("falling")) d_ff_1 (.clk(CLK), .D(READY_INST), .Q(d_ff_1_q));  // open: Qn, preset, en, reset
  D_Flip_Flop #(.trigger("falling")) d_ff_2 (
    .clk(CLK), .D(demultiplexer_1_out1), .Q(d_ff_2_q), .reset(RST));  // open: Qn, preset, en
  or or_1 (RF, d_ff_2_q, READY_DATA, RF_t);
  and and_1 (TTY_EN, KBD_EN, TTY_INST);
  Priority_Encoder priority_encoder_1 (
    .in0(1'b1), .in1(ALU_INST), .in2(JMP_INST), .in3(R_INST), .in4(MEM_INST), .in5(WRITE_INST),
    .out(Selector), .en_in(1'b1));  // open: in6, in7, gs, en_out
  D_Flip_Flop #(.trigger("falling")) d_ff_3 (.clk(CLK), .D(RF), .Q(KBD_EN));  // open: Qn, preset, en, reset
  or or_2 (or_2_out, END, Idle);
  D_Flip_Flop #(.trigger("falling")) d_ff_4 (.clk(CLK), .D(or_2_out), .Q(END), .reset(RST));  // open: Qn, preset, en
  or or_3 (PC, KBD_EN, READY_WRITE, Branch);
  D_Flip_Flop #(.trigger("falling")) d_ff_5 (.clk(CLK), .D(START), .Q(d_ff_5_q), .reset(RST));  // open: Qn, preset, en
  or or_4 (GET_INST, d_ff_5_q, d_ff_6_q);
  D_Flip_Flop #(.trigger("falling")) d_ff_6 (.clk(CLK), .D(PC), .Q(d_ff_6_q), .reset(RST));  // open: Qn, preset, en

  assign UseGI = READY_INST;

  // Other names for the same wires on the sheet: AluInst = ALU_INST; getInst = GET_INST; JmpInst = JMP_INST;
  //   MemInst = MEM_INST; Read = GET_DATA; ReadyData = READY_DATA; ReadyInst = READY_INST; ReadyW = READY_WRITE;
  //   Reset = RST; RInst = R_INST; KbdEn = KBD_EN; Tty = KBD_EN; TtyEn = TTY_EN; TtyInst = TTY_INST; usePC = PC;
  //   useRF = RF; WriteInst = WRITE_INST

  // Notes on the sheet:
  //   Entradas
  //   Salidas
  //   Enable Terminal
  //   Idle
endmodule

module Using_RAM (
  input  [31:0] in_1,
  input  [31:0] in_2,
  input  [31:0] in_3,
  input  [31:0] in_4,
  input  [31:0] in_5,
  input  [3:0] in_6,
  input  [3:0] in_7,
  input  in_8,
  input  in_9,
  input  in_10,
  input  in_11,
  input  in_12,
  input  is_inst,
  output [31:0] out_14,
  output [31:0] out_15,
  output [31:0] out_16,
  output [31:0] out_17,
  output [15:0] out_18,
  output [3:0] out_19,
  output out_20,
  output out_21,
  output out_22,
  output out_23,
  output out_24
);

  wire CSD, CSI, or_1_out, Stop0;
  wire [31:0] DO0, DO1, DO2, DO3, inverter_1_output, inverter_2_output, inverter_3_output, inverter_4_output,
       IO0, IO1, IO2, IO3;

  or or_1 (or_1_out, in_10, Stop0);
  or or_2 (out_21, CSI, out_20, CSD);
  D_Flip_Flop #(.trigger("falling")) d_ff_1 (
    .clk(in_8), .D(in_10), .Q(out_20), .en(or_1_out));  // open: Qn, preset, reset
  Cronometro cronometro_1 (.start(out_20), .rst(out_24), .clk(in_8), .\time (in_6), .Ready(Stop0));
  Access_RAM access_ram_1 (
    .in_1(in_1), .in_2(in_2), .in_3(in_3), .in_4(in_4), .in_10(in_7), .in_6(in_8), .in_7(in_9), .in_8(in_11),
    .out_11(IO0), .out_12(IO1), .out_13(IO2), .out_14(IO3), .out_15(CSI), .out_16(out_22), .in_5(in_5[19:4]),
    .in_9(in_10));
  Access_RAM access_ram_2 (
    .in_1(in_1), .in_2(in_2), .in_3(in_3), .in_4(in_4), .in_10(in_7), .in_6(in_8), .in_7(in_9), .in_8(in_12),
    .out_11(DO0), .out_12(DO1), .out_13(DO2), .out_14(DO3), .out_15(CSD), .out_16(out_23), .in_5(in_5[19:4]),
    .in_9(in_10));
  Demultiplexer #(.select(2)) demultiplexer_1 (
    .out0(out_19[0]), .out1(out_19[1]), .out2(out_19[2]), .out3(out_19[3]), .in(1'b1), .sel(in_5[3:2]));  // open: en
  D_Flip_Flop #(.trigger("falling")) d_ff_2 (.clk(in_8), .D(Stop0), .Q(out_24));  // open: Qn, preset, en, reset
  Multiplexer #(.width(32)) multiplexer_1 (
    .in0(inverter_1_output), .in1(IO3), .out(out_17), .sel(is_inst));  // open: en
  Multiplexer #(.width(32)) multiplexer_2 (
    .in0(inverter_2_output), .in1(IO0), .out(out_14), .sel(is_inst));  // open: en
  Multiplexer #(.width(32)) multiplexer_3 (
    .in0(inverter_3_output), .in1(IO1), .out(out_15), .sel(is_inst));  // open: en
  Multiplexer #(.width(32)) multiplexer_4 (
    .in0(inverter_4_output), .in1(IO2), .out(out_16), .sel(is_inst));  // open: en
  Inverter inverter_1 (.in_1(DO3), .Output(inverter_1_output));
  Inverter inverter_2 (.in_1(DO0), .Output(inverter_2_output));
  Inverter inverter_3 (.in_1(DO1), .Output(inverter_3_output));
  Inverter inverter_4 (.in_1(DO2), .Output(inverter_4_output));

  assign out_18 = in_5[19:4];

  // Other names for the same wires on the sheet: Bank0[31:0] = in_1; Bank1[31:0] = in_2; Bank2[31:0] = in_3;
  //   Bank3[31:0] = in_4; BankOut0[31:0] = out_14; BankOut1[31:0] = out_15; BankOut2[31:0] = out_16;
  //   BankOut3[31:0] = out_17; Clk = in_8; CS = out_21; DPAddress[31:0] = in_5; ADDR[15:0] = in_5[19:4];
  //   getData = in_12; getInst = in_11; isInst = is_inst; MASK[3:0] = out_19; ReadTime[3:0] = in_7;
  //   ReadyData = out_23; ReadyInst = out_22; ReadyWrite = out_24; Reset = in_9; RW = out_20; Write = in_10;
  //   WriteTime[3:0] = in_6

  // Notes on the sheet:
  //   Entradas
  //   Devuelve la instrucción
  //   Devuelve de memoria cuando no es instrucción
  //   Carga si es instrucción o datos de la ram
  //   Salidas
endmodule

module Access_RAM (
  input  [31:0] in_1,
  input  [31:0] in_2,
  input  [31:0] in_3,
  input  [31:0] in_4,
  input  [15:0] in_5,
  input  in_6,
  input  in_7,
  input  in_8,
  input  in_9,
  input  [3:0] in_10,
  output [31:0] out_11,
  output [31:0] out_12,
  output [31:0] out_13,
  output [31:0] out_14,
  output out_15,
  output out_16
);

  wire a, and_1_out, and_4_out, comparator_1_eq, Cont, d_ff_3_q, getRead, multiplexer_1_out, not_1_out,
       or_1_out, ReadyRead, ResetMem, RM, save_Instr, Stop;
  wire [15:0] ADDRMem;

  Register #(.width(32)) register_1 (.D(in_1), .en(save_Instr), .Q(out_11), .clk(in_6), .clr(in_7));
  Register #(.width(32)) register_2 (.D(in_2), .en(save_Instr), .Q(out_12), .clk(in_6), .clr(in_7));
  Register #(.width(32)) register_3 (.D(in_3), .en(save_Instr), .Q(out_13), .clk(in_6), .clr(in_7));
  Register #(.width(32)) register_4 (.D(in_4), .en(save_Instr), .Q(out_14), .clk(in_6), .clr(in_7));
  D_Flip_Flop #(.trigger("falling")) d_ff_1 (.clk(in_6), .D(getRead), .Q(a), .en(or_1_out));  // open: Qn, preset, reset
  or or_1 (or_1_out, getRead, Stop);
  Register #(.width(16)) register_5 (.D(in_5), .en(save_Instr), .Q(ADDRMem), .clk(in_6), .clr(in_7));
  Multiplexer #(.enable("false")) multiplexer_1 (.in0(ResetMem), .in1(RM), .out(multiplexer_1_out), .sel(RM));
  and and_1 (and_1_out, in_8, Cont);
  D_Flip_Flop #(.trigger("falling")) d_ff_2 (
    .clk(in_6), .D(multiplexer_1_out), .Q(ResetMem), .reset(ReadyRead));  // open: Qn, preset, en
  and and_2 (getRead, in_8, not_1_out);
  not not_1 (not_1_out, Cont);
  D_Flip_Flop #(.trigger("falling")) d_ff_3 (
    .clk(in_6), .D(and_1_out), .Q(d_ff_3_q), .reset(in_7));  // open: Qn, preset, en
  Comparator #(.width(16)) comparator_1 (.a(in_5), .b(ADDRMem), .eq(comparator_1_eq));  // open: gt, lt
  Cronometro cronometro_1 (.start(a), .rst(ReadyRead), .clk(in_6), .\time (in_10), .Ready(Stop));
  or or_2 (out_16, d_ff_3_q, ReadyRead);
  and and_3 (Cont, ~ResetMem, comparator_1_eq);  // AND_Gate
  D_Flip_Flop #(.trigger("falling")) d_ff_4 (
    .clk(in_6), .D(Stop), .Q(save_Instr), .reset(ReadyRead));  // open: Qn, preset, en
  and and_4 (and_4_out, in_9, Cont);
  D_Flip_Flop #(.trigger("falling")) d_ff_5 (.clk(in_6), .D(save_Instr), .Q(ReadyRead));  // open: Qn, preset, en, reset
  or or_3 (RM, and_4_out, in_7);
  or or_4 (out_15, save_Instr, a);

  // Other names for the same wires on the sheet: ADDR[15:0] = in_5; Bank0[31:0] = in_1; Bank1[31:0] = in_2;
  //   Bank2[31:0] = in_3; Bank3[31:0] = in_4; BankOut0[31:0] = out_11; BankOut1[31:0] = out_12;
  //   BankOut2[31:0] = out_13; BankOut3[31:0] = out_14; Clk = in_6; CS = out_15; get = in_8; ReadTime[3:0] = in_10;
  //   Ready = out_16; Reset = in_7; Write = in_9

  // Notes on the sheet:
  //   Entradas
  //   Banks
  //   Salidas
  //   Address
  //   Ready leer
  //   Espera el tiempo de lectura para leer de memoria
  //   Resetear el contador del tiempo de lectura
  //   Chip Select
endmodule

module Branch_Control (
  input  beq,
  input  [25:0] Dest,
  input  bne,
  input  blez,
  input  bgtz,
  input  [15:0] Const,
  input  bltz,
  input  jr,
  input  j,
  input  [31:0] RS,
  input  [31:0] RT,
  input  [31:0] PC,
  output [31:0] OUT
);

  wire and_1_out, and_2_out, and_3_out, and_4_out, and_5_out, comparator_1_eq, or_2_out, RS_0, RS__0, RS__RT;
  wire [1:0] code;
  wire [13:0] bit_extender_1_out;
  wire [31:0] PC_4, PC_4_Offset;

  Adder #(.width(32)) adder_1 (.a(PC), .b(32'h4), .out(PC_4));  // open: cin, cout
  assign bit_extender_1_out = {{13{Const[15]}}, Const[15]};  // Bit_Extender bit_extender_1
  Comparator #(.width(32)) comparator_1 (.a(RS), .b({32{1'b0}}), .eq(comparator_1_eq), .lt(RS_0));  // open: gt
  Adder #(.width(32)) adder_2 (.a(PC_4), .b({bit_extender_1_out, Const, 2'b00}), .out(PC_4_Offset));  // open: cin, cout
  or or_1 (RS__0, comparator_1_eq, RS_0);
  Comparator #(.width(32)) comparator_2 (.a(RS), .b(RT), .eq(RS__RT));  // open: gt, lt
  Multiplexer #(.select(2), .width(32)) multiplexer_1 (
    .in0(PC_4), .in1(PC_4_Offset), .in2({PC[31:28], Dest, 2'b00}), .in3(RS), .out(OUT), .sel(code));  // open: en
  and and_1 (and_1_out, beq, RS__RT);
  and and_2 (and_2_out, ~RS__RT, bne);  // AND_Gate
  and and_3 (and_3_out, blez, RS__0);
  and and_4 (and_4_out, ~RS__0, bgtz);  // AND_Gate
  and and_5 (and_5_out, bltz, RS_0);
  or or_2 (or_2_out, and_1_out, and_2_out, and_3_out, and_4_out, and_5_out);
  Priority_Encoder #(.select(2)) priority_encoder_1 (
    .in0(1'b1), .in1(or_2_out), .in2(j), .in3(jr), .out(code), .en_in(1'b1));  // open: gs, en_out
  // Probe on code

  // Other names for the same wires on the sheet: Offset[15:0] = Const; Jmp[31:2] = {PC[31:28], Dest}

  // Notes on the sheet:
  //   Entradas
  //   Instrucción normal
  //   Instrucción jump
  //   Salida
  //   Selector:
  //   11 jr
  //   00 normal
  //   01 branch
  //   10 jump
endmodule

module Memory_Address (
  input  [31:0] PC,
  input  [31:0] ALU,
  input  [31:0] SP,
  input  LW,
  input  SW,
  input  POP,
  input  PUSH,
  input  IS_PC,
  output [31:0] OUT
);

  wire or_1_out, or_2_out;
  wire [1:0] priority_encoder_1_out;
  wire [31:0] multiplexer_1_out, subtractor_1_out;

  Multiplexer #(.width(32)) multiplexer_1 (
    .in0(SP), .in1(subtractor_1_out), .out(multiplexer_1_out), .sel(PUSH));  // open: en
  Subtractor #(.width(32)) subtractor_1 (.a(SP), .b(32'h4), .out(subtractor_1_out));  // open: bin, bout
  or or_1 (or_1_out, SW, LW);
  or or_2 (or_2_out, POP, PUSH);
  Priority_Encoder #(.select(2)) priority_encoder_1 (
    .in0(1'b1), .in1(or_1_out), .in2(or_2_out), .in3(IS_PC), .out(priority_encoder_1_out), .en_in(1'b1));  // open: gs, en_out
  Multiplexer #(.select(2), .width(32)) multiplexer_2 (
    .in0(PC), .in1(ALU), .in2(multiplexer_1_out), .in3(PC), .out(OUT), .sel(priority_encoder_1_out));  // open: en

  // Other names for the same wires on the sheet: isPC = IS_PC

  // Notes on the sheet:
  //   Entradas
  //   Salida
endmodule

module Multiplication (
  input  Sign,
  input  [31:0] A,
  input  [31:0] B,
  output [31:0] OH,
  output [31:0] OL
);

  wire and_1_out, Overflow, Overflow1, SigX, SigY, sr_2__31, sr_3__31;
  wire [31:0] NA, NAA, NB, NBB, OH1, OH2, OL1, OL2, RH, RH1, RL, RL1, sl_1_sl, sl_2_sl, sr_1_sr, sr_6_sr,
       sr_7_sr, subtractor_1_out, SumX, SumY;

  and and_1 (and_1_out, SigX, SigY);
  SR sr_1 (.In({32{1'b0}}), .new_bit_0(and_1_out), .SR(sr_1_sr));  // open: _31
  Multiplexer #(.width(32), .enable("false")) multiplexer_1 (
    .in0({32{1'b0}}), .in1(subtractor_1_out), .out(SumX), .sel(SigY));
  Subtractor #(.width(32)) subtractor_1 (.a(A), .b(sr_1_sr), .out(subtractor_1_out));  // open: bin, bout
  Multiplier #(.width(32)) multiplier_1 (.a(A), .b(B), .out(OL1), .cout(OH1));  // open: cin
  SR sr_2 (.In(OL2), .new_bit_0(1'b0), ._31(sr_2__31), .SR(NA));
  SR sr_3 (.In(NA), .new_bit_0(1'b0), ._31(sr_3__31), .SR(NAA));
  Multiplexer #(.width(32), .enable("false")) multiplexer_2 (.in0({32{1'b0}}), .in1(B), .out(SumY), .sel(SigX));
  SL sl_1 (.IN(A), .new_bit_31(1'b0), .bit_0(SigX), .SL(sl_1_sl));
  SL sl_2 (.IN(B), .new_bit_31(1'b0), .bit_0(SigY), .SL(sl_2_sl));
  SR sr_4 (.In(OH2), .new_bit_0(sr_2__31), .SR(NB));  // open: _31
  SR sr_5 (.In(NB), .new_bit_0(sr_3__31), .SR(NBB));  // open: _31
  Multiplier #(.width(32)) multiplier_2 (.a(sl_1_sl), .b(sl_2_sl), .out(OL2), .cout(OH2));  // open: cin
  Adder #(.width(32)) adder_1 (.a(NAA), .b(SumX), .out(RL), .cout(Overflow));  // open: cin
  Adder #(.width(32)) adder_2 (.a(RL), .b(SumY), .out(RL1), .cout(Overflow1));  // open: cin
  Multiplexer #(.width(32), .enable("false")) multiplexer_3 (.in0(RH1), .in1(OH1), .out(OH), .sel(Sign));
  Multiplexer #(.width(32), .enable("false")) multiplexer_4 (.in0(RL1), .in1(OL1), .out(OL), .sel(Sign));
  SR sr_6 (.In({32{1'b0}}), .new_bit_0(Overflow), .SR(sr_6_sr));  // open: _31
  SR sr_7 (.In({32{1'b0}}), .new_bit_0(Overflow1), .SR(sr_7_sr));  // open: _31
  Adder #(.width(32)) adder_3 (.a(NBB), .b(sr_6_sr), .out(RH));  // open: cin, cout
  Adder #(.width(32)) adder_4 (.a(RH), .b(sr_7_sr), .out(RH1));  // open: cin, cout

  // Other names for the same wires on the sheet: X[31:0] = A; Y[31:0] = B

  // Notes on the sheet:
  //   Casos:
  //   Si y termina en 0, SumX va a ser 0
  //   Si x y y terminan en 1, se le resta uno a X
  //   Si x termina en 0 y y en 1 SumX será X
  //   Mult normal
  //   Si x termina en 1, sumY sera Y, sino 0
endmodule

module Division (
  input  [31:0] Op1,
  input  [31:0] Op2,
  input  Sign,
  output [31:0] DivRem,
  output [31:0] Div
);

  wire SignX, SignY;
  wire [31:0] negator_1_out, negator_2_out, X1, Y1;

  and and_1 (SignX, Sign, Op1[31]);
  and and_2 (SignY, Sign, Op2[31]);
  Divider #(.width(32)) divider_1 (.a(X1), .b(Y1), .out(Div), .rem(DivRem));  // open: upper
  Negator #(.width(32)) negator_1 (.in(Op1), .out(negator_1_out));
  Negator #(.width(32)) negator_2 (.in(Op2), .out(negator_2_out));
  Multiplexer #(.width(32)) multiplexer_1 (.in0(Op1), .in1(negator_1_out), .out(X1), .sel(SignX));  // open: en
  Multiplexer #(.width(32)) multiplexer_2 (.in0(Op2), .in1(negator_2_out), .out(Y1), .sel(SignY));  // open: en

  // Other names for the same wires on the sheet: Rem[31:0] = DivRem

  // Notes on the sheet:
  //   Entradas
  //   Salidas
  //   Si es div con signo y es negativo sgn se activa
  //   Si sgn esta activo se elige compa2
  //   Division Normal
endmodule

module Less_Than (
  input  [31:0] A,
  input  [31:0] B,
  input  sign,
  output Less_Than
);

  wire comparator_1_lt, comparator_2_lt, LT1, LT2;

  Comparator #(.width(32)) comparator_1 (.a(A), .b(B), .lt(comparator_1_lt));  // open: gt, eq
  Comparator #(.width(32), .mode("unsigned")) comparator_2 (.a(A), .b(B), .lt(comparator_2_lt));  // open: gt, eq
  and and_1 (LT1, comparator_1_lt, sign);
  and and_2 (LT2, ~sign, comparator_2_lt);  // AND_Gate
  or or_1 (Less_Than, LT1, LT2);

  // Notes on the sheet:
  //   Se activa si A es menor que B sea con signo o no
endmodule

module SL (
  input  [31:0] IN,
  input  new_bit_31,
  output bit_0,
  output [31:0] SL
);


  assign bit_0 = IN[0];
  assign SL = {new_bit_31, IN[31:1]};
endmodule

module SR (
  input  new_bit_0,
  input  [31:0] In,
  output [31:0] SR,
  output _31
);


  assign _31 = In[31];
  assign SR = {In[30:0], new_bit_0};
endmodule

module Inverter (
  input  [31:0] in_1,
  output [31:0] Output
);


  assign Output = {in_1[7:0], in_1[15:8], in_1[23:16], in_1[31:24]};

  // Notes on the sheet:
  //   Invertir el orden de los bits
endmodule

module Cronometro (
  input  [3:0] \time ,
  input  start,
  input  clk,
  input  rst,
  output Ready
);

  wire [3:0] counter_1_q;

  Counter #(.width(4), .max('hf)) counter_1 (
    .count(start), .Q(counter_1_q), .clk(clk), .clr(rst));  // open: load, D, carry
  Comparator #(.width(4)) comparator_1 (.a(\time ), .b(counter_1_q), .eq(Ready));  // open: gt, lt

  // Notes on the sheet:
  //   Se activa cuando llega a time
endmodule

module Const_Ext (
  input  ori,
  input  andi,
  input  [15:0] \const ,
  input  xori,
  output [31:0] Extended
);

  and and_1 (Extended[31], ~xori, ~andi, ~ori, \const [15]);  // AND_Gate

  assign Extended[30:0] = {{15{Extended[31]}}, \const };

  // Notes on the sheet:
  //   Extender la constante
endmodule

module G_Instruction (
  input  [31:0] in_1,
  input  in_2,
  input  in_3,
  input  in_4,
  output [31:0] Output
);

  wire [31:0] inverter_1_output;

  Inverter inverter_1 (.in_1(in_1), .Output(inverter_1_output));
  Register #(.width(32)) register_1 (.D(inverter_1_output), .en(in_2), .Q(Output), .clk(in_3), .clr(in_4));

  // Other names for the same wires on the sheet: Clk = in_3; Enable = in_2; Reset = in_4
endmodule
